// Logisim project 1220439_1220785.circ as structural Verilog: 5 circuits, main circuit main
module main (
);

  wire clk_out, ExtOP, MemRead, MemWrite, RegDst, RegWrite;
  wire [1:0] BSel, f, PCSel, WriteBack;
  wire [2:0] Imm3, multiplexer_2_out;
  wire [3:0] AluOP;
  wire [4:0] OP, shifter_1_out;
  wire [4:2] Imm5;
  wire [7:5] Imm11;
  wire [10:0] shifter_2_out, shifter_3_out;
  wire [19:0] adder_1_out, adder_2_out, bit_extender_1_out, bit_extender_2_out, multiplexer_1_out, PC, PC_2,
       undriven;
  wire [31:0] alu_1_output, bit_extender_5_out, bit_extender_6_out, bit_extender_7_out, Bus_X, Bus_Y,
       multiplexer_3_out, multiplexer_4_out, ram_1_data, sExtImm5, undriven_2, zExtImm5;

  Shifter #(.width(5)) shifter_1 (.in({Imm5, f}), .\dist (3'b001), .out(shifter_1_out));
  assign bit_extender_1_out = {{15{1'b0}}, shifter_1_out};  // Bit_Extender bit_extender_1
  ControlUnit controlunit_1 (
    .OPCode(OP), .RegDst(RegDst), .RegWrite(RegWrite), .ExtOP(ExtOP), .BSel(BSel), .MemWrite(MemWrite),
    .MemRead(MemRead), .WriteBack(WriteBack), .ALU_OP(AluOP), .f(f));
  Shifter #(.width(11)) shifter_2 (.in({Imm3, Imm11, Imm5, f}), .\dist (4'b0001), .out(shifter_2_out));
  Adder #(.width(20)) adder_1 (.a(PC), .b(bit_extender_1_out), .out(adder_1_out));  // open: cin, cout
  assign bit_extender_2_out = {{9{1'b0}}, shifter_2_out};  // Bit_Extender bit_extender_2
  Adder #(.width(20)) adder_2 (.a(PC), .b(bit_extender_2_out), .out(adder_2_out));  // open: cin, cout
  Multiplexer #(.select(2), .width(20), .enable("false")) multiplexer_1 (
    .in0(PC_2), .in1(adder_1_out), .in2(adder_2_out), .in3(undriven), .out(multiplexer_1_out), .sel(PCSel));
  Clock clk (.out(clk_out));
  Register #(.width(20)) u_PC (.D(multiplexer_1_out), .en(1'b1), .Q(PC), .clk(clk_out));  // open: clr
  PC_CU pc_cu_1 (.OP_Code(OP), .X(Imm3), .Y(Imm11), .PCSel(PCSel));
  Adder #(.width(20)) adder_3 (.a(PC), .b(20'h2), .out(PC_2));  // open: cin, cout
  ROM #(.addrWidth(20), .dataWidth(16)) rom_1 (.addr(PC), .data({OP, Imm3, Imm11, Imm5, f}));  // open: sel
  assign zExtImm5 = {{27{1'b0}}, {Imm5, f}};  // Bit_Extender bit_extender_3
  assign sExtImm5 = {{27{Imm5[4]}}, {Imm5, f}};  // Bit_Extender bit_extender_4
  REG reg_1 (
    .Rz(Imm5), .Ry(Imm11), .BusX(Bus_X), .Rx(multiplexer_2_out), .Clock(clk_out), .REG(RegWrite),
    .BusY(Bus_Y), .BusZ(undriven_2));
  Multiplexer #(.width(3), .enable("false")) multiplexer_2 (
    .in0(Imm3), .in1(3'b111), .out(multiplexer_2_out), .sel(RegDst));
  Multiplexer #(.width(32), .enable("false")) multiplexer_3 (
    .in0(zExtImm5), .in1(sExtImm5), .out(multiplexer_3_out), .sel(ExtOP));
  Shifter #(.width(11)) shifter_3 (.in({Imm3, Imm11, Imm5, f}), .\dist (4'b0001), .out(shifter_3_out));
  assign bit_extender_5_out = {{27{1'b0}}, {f, Imm3}};  // Bit_Extender bit_extender_5
  assign bit_extender_6_out = {{21{1'b0}}, shifter_3_out};  // Bit_Extender bit_extender_6
  Multiplexer #(.select(2), .width(32), .enable("false")) multiplexer_4 (
    .in0(undriven_2), .in1(multiplexer_3_out), .in2(bit_extender_5_out), .in3(bit_extender_6_out),
    .out(multiplexer_4_out), .sel(BSel));
  ALU alu_1 (.Y(Bus_Y), .Z(multiplexer_4_out), .Output(alu_1_output), .selctorALU(AluOP));
  RAM #(.addrWidth(20), .dataWidth(32), .bus("separate")) ram_1 (
    .addr(alu_1_output[19:0]), .din(undriven_2), .data(ram_1_data), .str(MemWrite), .clk(clk_out),
    .ld(MemRead));  // open: sel, clr
  assign bit_extender_7_out = {{12{PC_2[19]}}, PC_2};  // Bit_Extender bit_extender_7
  Multiplexer #(.select(2), .width(32), .enable("false")) multiplexer_5 (
    .in0(alu_1_output), .in1(ram_1_data), .in2(bit_extender_7_out), .out(Bus_X), .sel(WriteBack));  // open: in3

  // Other names for the same wires on the sheet: Imm11 (some bits) = {Imm3, Imm5, f}; Z[2:0] = Imm5; Y[2:0] = Imm11;
  //   X[2:0] = Imm3; Imm2[1:0] = f; Imm5[1:0] = f

  // Notes on the sheet:
  //   InstMemo
  //   J Type
  //   I Type
  //   R Type
  //   S Type
endmodule

module ALU (
  input  [31:0] Y,
  input  [31:0] Z,
  input  [3:0] selctorALU,
  output [31:0] Output
);

  wire comparator_1_eq, comparator_2_lt;
  wire [31:0] adder_1_out, and_1_out, and_2_out, bit_extender_1_out, bit_extender_2_out, not_1_out, or_1_out,
       shifter_1_out, shifter_2_out, shifter_3_out, shifter_4_out, subtractor_1_out, undriven, xor_1_out;

  assign not_1_out = ~Y;  // NOT_Gate not_1, 32 bits wide
  assign xor_1_out = Y ^ Z;  // XOR_Gate xor_1, 32 bits wide
  assign and_1_out = Y & Z;  // AND_Gate and_1, 32 bits wide
  assign or_1_out = Y | Z;  // OR_Gate or_1, 32 bits wide
  assign and_2_out = not_1_out & Z;  // AND_Gate and_2, 32 bits wide
  Adder #(.width(32)) adder_1 (.a(Y), .b(Z), .out(adder_1_out));  // open: cin, cout
  Comparator #(.width(32)) comparator_1 (.a(Y), .b(Z), .eq(comparator_1_eq));  // open: gt, lt
  Subtractor #(.width(32)) subtractor_1 (.a(Z), .b(Y), .out(subtractor_1_out));  // open: bin, bout
  Comparator #(.width(32)) comparator_2 (.a(Y), .b(Z), .lt(comparator_2_lt));  // open: gt, eq
  assign bit_extender_1_out = {{31{1'b0}}, comparator_1_eq};  // Bit_Extender bit_extender_1
  assign bit_extender_2_out = {{31{1'b0}}, comparator_2_lt};  // Bit_Extender bit_extender_2
  Shifter #(.width(32), .shift("ar")) shifter_1 (.in(Y), .\dist (Z[4:0]), .out(shifter_1_out));
  Shifter #(.width(32), .shift("lr")) shifter_2 (.in(Y), .\dist (Z[4:0]), .out(shifter_2_out));
  Shifter #(.width(32)) shifter_3 (.in(Y), .\dist (Z[4:0]), .out(shifter_3_out));
  Shifter #(.width(32), .shift("rr")) shifter_4 (.in(Y), .\dist (Z[4:0]), .out(shifter_4_out));
  Multiplexer #(.select(4), .width(32)) multiplexer_1 (
    .in0(xor_1_out), .in1(and_1_out), .in2(or_1_out), .in3(and_2_out), .in4(adder_1_out),
    .in5(bit_extender_1_out), .in6(subtractor_1_out), .in7(bit_extender_2_out), .in8(shifter_1_out),
    .in9(shifter_2_out), .in10(shifter_3_out), .in11(shifter_4_out), .in12(undriven), .in13(undriven),
    .in14(undriven), .in15(undriven), .out(Output), .sel(selctorALU));  // open: en

  // Notes on the sheet:
  //   Splitter
  //   0-4
  //   ArthmeticRight
  //   RightLogical
  //   LeftLogical
  //   BitExtender1
  //   BitExtender2
  //   RptateRight
endmodule

module REG (
  input  [2:0] Rz,
  input  [2:0] Ry,
  input  [31:0] BusX,
  input  [2:0] Rx,
  input  Clock,
  input  REG,
  input  [31:0] BusY,
  input  [31:0] BusZ
);

  wire and_1_out, and_2_out, and_3_out, and_4_out, and_5_out, and_6_out, and_7_out, decoder_1_out0,
       decoder_2_out0, decoder_2_out1, decoder_2_out2, decoder_2_out3, decoder_2_out4, decoder_2_out5,
       decoder_2_out6, decoder_2_out7, decoder_3_out0, decoder_3_out1, decoder_3_out2, decoder_3_out3,
       decoder_3_out4, decoder_3_out5, decoder_3_out6, decoder_3_out7, reg1, reg2, reg3, reg4, reg5, reg6,
       reg7;
  wire [31:0] R1_q, R2_q, R3_q, R4_q, R5_q, R6_q, R7_q;

  Decoder #(.select(3)) decoder_1 (
    .out0(decoder_1_out0), .out1(reg1), .out2(reg2), .out3(reg3), .out4(reg4), .out5(reg5), .out6(reg6),
    .out7(reg7), .sel(Rx));  // open: en
  and and_1 (and_1_out, reg1, REG);
  and and_2 (and_2_out, reg2, REG);
  and and_3 (and_3_out, reg3, REG);
  and and_4 (and_4_out, reg4, REG);
  and and_5 (and_5_out, reg5, REG);
  and and_6 (and_6_out, reg6, REG);
  and and_7 (and_7_out, reg7, REG);
  Register #(.width(32)) R1 (.D(BusX), .en(and_1_out), .Q(R1_q), .clk(Clock));  // open: clr
  Register #(.width(32)) R2 (.D(BusX), .en(and_2_out), .Q(R2_q), .clk(Clock));  // open: clr
  Register #(.width(32)) R3 (.D(BusX), .en(and_3_out), .Q(R3_q), .clk(Clock));  // open: clr
  Register #(.width(32)) R4 (.D(BusX), .en(and_4_out), .Q(R4_q), .clk(Clock));  // open: clr
  Register #(.width(32)) R5 (.D(BusX), .en(and_5_out), .Q(R5_q), .clk(Clock));  // open: clr
  Register #(.width(32)) R6 (.D(BusX), .en(and_6_out), .Q(R6_q), .clk(Clock));  // open: clr
  Register #(.width(32)) R7 (.D(BusX), .en(and_7_out), .Q(R7_q), .clk(Clock));  // open: clr
  Decoder #(.select(3)) decoder_2 (
    .out0(decoder_2_out0), .out1(decoder_2_out1), .out2(decoder_2_out2), .out3(decoder_2_out3),
    .out4(decoder_2_out4), .out5(decoder_2_out5), .out6(decoder_2_out6), .out7(decoder_2_out7), .sel(Ry));  // open: en
  assign BusY = decoder_2_out0 ? {32{1'b0}} : 32'bz;  // Controlled_Buffer controlled_buffer_1
  assign BusY = decoder_2_out1 ? R1_q : 32'bz;  // Controlled_Buffer controlled_buffer_2
  assign BusY = decoder_2_out2 ? R2_q : 32'bz;  // Controlled_Buffer controlled_buffer_3
  assign BusY = decoder_2_out3 ? R3_q : 32'bz;  // Controlled_Buffer controlled_buffer_4
  assign BusY = decoder_2_out4 ? R4_q : 32'bz;  // Controlled_Buffer controlled_buffer_5
  assign BusY = decoder_2_out5 ? R5_q : 32'bz;  // Controlled_Buffer controlled_buffer_6
  assign BusY = decoder_2_out6 ? R6_q : 32'bz;  // Controlled_Buffer controlled_buffer_7
  assign BusY = decoder_2_out7 ? R7_q : 32'bz;  // Controlled_Buffer controlled_buffer_8
  Decoder #(.select(3)) decoder_3 (
    .out0(decoder_3_out0), .out1(decoder_3_out1), .out2(decoder_3_out2), .out3(decoder_3_out3),
    .out4(decoder_3_out4), .out5(decoder_3_out5), .out6(decoder_3_out6), .out7(decoder_3_out7), .sel(Rz));  // open: en
  assign BusZ = decoder_3_out0 ? {32{1'b0}} : 32'bz;  // Controlled_Buffer controlled_buffer_9
  assign BusZ = decoder_3_out1 ? R1_q : 32'bz;  // Controlled_Buffer controlled_buffer_10
  assign BusZ = decoder_3_out2 ? R2_q : 32'bz;  // Controlled_Buffer controlled_buffer_11
  assign BusZ = decoder_3_out3 ? R3_q : 32'bz;  // Controlled_Buffer controlled_buffer_12
  assign BusZ = decoder_3_out4 ? R4_q : 32'bz;  // Controlled_Buffer controlled_buffer_13
  assign BusZ = decoder_3_out5 ? R5_q : 32'bz;  // Controlled_Buffer controlled_buffer_14
  assign BusZ = decoder_3_out6 ? R6_q : 32'bz;  // Controlled_Buffer controlled_buffer_15
  assign BusZ = decoder_3_out7 ? R7_q : 32'bz;  // Controlled_Buffer controlled_buffer_16
endmodule

module ControlUnit (
  input  [4:0] OPCode,
  input  [1:0] f,
  output [1:0] WriteBack,
  output MemRead,
  output MemWrite,
  output [1:0] BSel,
  output ExtOP,
  output RegWrite,
  output RegDst,
  output [3:0] ALU_OP
);

  ROM #(.addrWidth(5), .dataWidth(9)) rom_1 (
    .addr(OPCode), .data({RegDst, RegWrite, ExtOP, BSel, MemWrite, MemRead, WriteBack}));  // open: sel
  ROM #(.addrWidth(7), .dataWidth(4)) rom_2 (.addr({OPCode, f}), .data(ALU_OP));  // open: sel

  // Notes on the sheet:
  //   Main Control Unit
  //   ALU Control Unit
  //   contents of rom_1 (hex, n*v repeats v):
  //   80 80 4*90 4*d0 4*90 4*d0 d4 39 e2 1e0
  //   contents of rom_2 (hex, n*v repeats v):
  //   1 4 2 0 3 5 6 7 8*0 4*2 4*0 4*3 12*0 4*a 4*9 4*8 4*b
endmodule

module PC_CU (
  input  [4:0] OP_Code,
  input  [2:0] X,
  input  [2:0] Y,
  output [1:0] PCSel
);

  wire comparator_1_gt, E, G, LE;

  Comparator #(.width(3)) comparator_1 (.a(X), .b(Y), .gt(comparator_1_gt), .eq(E), .lt(G));
  ROM #(.dataWidth(2)) rom_1 (.addr({OP_Code, LE, E, G}), .data(PCSel));  // open: sel
  or or_1 (LE, comparator_1_gt, E);

  // Notes on the sheet:
  //   Less than or Equal
  //   Equal
  //   Greater than
  //   PC Control Unit
  //   contents of rom_1 (hex, n*v repeats v):
  //   118*0 1 0 0 1 0 0 1 5*0 1 9*0 1 20*0 2 0 0 2 0 2 0 0 2 0 0 2 67*0 1 0 0 1
endmodule
